# Fritzing sketch Flickerfusion Schematic (saved by Fritzing 0.9.3b)
breadboards: 1

parts:
  Teensy_3_1 = Teensy 3.1
  LED1 = smd LED [color="Red (633nm)" package="0805 [SMD]"]
  S1 = Pushbutton [package="[SMD]"]
  R3 = Resistor [tolerance=±5% resistance=330 package=THT]

nets:
  N1: Teensy_3_1.GND, LED1.cathode, S1.Pin_1, S1.Pin_2
  N2: Teensy_3_1.D5, S1.Pin_3, S1.Pin_4
  N3: Teensy_3_1.D12, R3.Pin_0
  N4: LED1.anode, R3.Pin_1
